# Fritzing sketch gps_1_schema (saved by Fritzing 0.8.5b)
breadboards: 1

parts:
  Composants1 = Arduino Leonardo (Rev3b)
  U1 = LCD-16X2 [package=lcd-16x2_noholes]
  RE1 = Rotary Encoder [package=THT]
  S1 = Pushbutton [package="[THT]"]
  R1 = TRIMPOT [package=trimpot-3mm]
  Composants2 = Arduino GPS Shield

nets:
  N1: Composants1.D0/RX, Composants2.UART_TX
  N2: Composants1.D1/TX, Composants2.UART_RX
  N3: Composants1.D5_PWM, U1.DB7
  N4: Composants1.D6_PWM/A7, U1.DB6
  N5: Composants1.D7, U1.DB5
  5V: Composants1.5V, U1.VDD, S1.Pin_1, S1.Pin_2, R1.CCW
  GND: Composants1.GND, U1.VSS, U1.R_W, U1.K, RE1.EncoderPinC, R1.CW
  N6: Composants1.A1, Composants2.D10
  N7: Composants1.D8/A8, U1.DB4
  N8: Composants1.D9_PWM/A9, S1.Pin_3, S1.Pin_4
  N9: Composants1.D10_PWM/A10, RE1.EncoderPinB
  N10: Composants1.D11_PWM, RE1.EncoderPinA
  N11: Composants1.D12/A11, U1.E
  N12: Composants1.D13_PWM, U1.RS
  N13: U1.VO, R1.WIPER
